// Logisim project cronometro.circ as structural Verilog: 8 circuits, main circuit main
module main (
  input  ENABLE,
  input  PRESET,
  input  CLEAR
);

  wire clock_1_out;
  wire [3:0] cronometro_1_hora_1_dezenas_minutos, cronometro_1_hora_1_dezenas_segundos,
       cronometro_1_hora_1_unidades_minutos, cronometro_1_hora_1_unidades_segundos;

  Clock clock_1 (.out(clock_1_out));
  Hex_Digit_Display hex_digit_display_1 (.value(cronometro_1_hora_1_dezenas_minutos));  // open: dp
  Hex_Digit_Display hex_digit_display_2 (.value(cronometro_1_hora_1_unidades_minutos));  // open: dp
  CRONOMETRO_1_HORA cronometro_1_hora_1 (
    .CLK(clock_1_out), .ENABLE(ENABLE), .PRESET(PRESET), .CLEAR(CLEAR),
    .DEZENAS_MINUTOS(cronometro_1_hora_1_dezenas_minutos),
    .UNIDADES_MINUTOS(cronometro_1_hora_1_unidades_minutos),
    .DEZENAS_SEGUNDOS(cronometro_1_hora_1_dezenas_segundos),
    .UNIDADES_SEGUNDOS(cronometro_1_hora_1_unidades_segundos));
  Hex_Digit_Display hex_digit_display_3 (.value(cronometro_1_hora_1_unidades_segundos));  // open: dp
  Hex_Digit_Display hex_digit_display_4 (.value(cronometro_1_hora_1_dezenas_segundos));  // open: dp

  // Notes on the sheet:
  //   minutos
  //   segundos
endmodule

module flip_flop_D (
  input  D,
  input  CLK,
  input  ENABLE,
  input  PRESET,
  input  CLEAR,
  output Q
);

  wire and_1_out, and_2_out, and_3_out, nor_2_out, not_1_out, not_2_out, not_3_out, not_4_out, or_1_out,
       or_2_out;

  not not_1 (not_1_out, CLK);
  not not_2 (not_2_out, not_1_out);
  not not_3 (not_3_out, not_2_out);
  and and_1 (and_1_out, not_3_out, CLK, ENABLE);
  not not_4 (not_4_out, D);
  and and_2 (and_2_out, not_4_out, and_1_out);
  and and_3 (and_3_out, and_1_out, D);
  or or_1 (or_1_out, CLEAR, and_2_out);
  or or_2 (or_2_out, and_3_out, PRESET);
  nor nor_1 (Q, or_1_out, nor_2_out);
  nor nor_2 (nor_2_out, Q, or_2_out);
endmodule

// SUM
module SOMADOR_DE_UM (
  input  CLK,
  input  ENABLE,
  input  PRESET,
  input  CLEAR,
  output [3:0] SAIDA
);

  wire [3:0] adder_1_out;

  flip_flop_D flip_flop_d_1 (
    .D(adder_1_out[3]), .CLK(CLK), .Q(SAIDA[3]), .ENABLE(ENABLE), .PRESET(PRESET), .CLEAR(CLEAR));
  Hex_Digit_Display hex_digit_display_1 (.value(SAIDA));  // open: dp
  flip_flop_D flip_flop_d_2 (
    .D(adder_1_out[2]), .CLK(CLK), .Q(SAIDA[2]), .ENABLE(ENABLE), .PRESET(PRESET), .CLEAR(CLEAR));
  flip_flop_D flip_flop_d_3 (
    .D(adder_1_out[1]), .CLK(CLK), .Q(SAIDA[1]), .ENABLE(ENABLE), .PRESET(PRESET), .CLEAR(CLEAR));
  flip_flop_D flip_flop_d_4 (
    .D(adder_1_out[0]), .CLK(CLK), .Q(SAIDA[0]), .ENABLE(ENABLE), .PRESET(PRESET), .CLEAR(CLEAR));
  Hex_Digit_Display hex_digit_display_2 (.value(adder_1_out));  // open: dp
  Adder #(.width(4)) adder_1 (.a(SAIDA), .b(4'b0001), .out(adder_1_out));  // open: cin, cout
endmodule

module CRONOMETRO_1_MIN (
  input  CLK,
  input  ENABLE,
  input  PRESET,
  input  CLEAR,
  output [3:0] UNIDADES,
  output [3:0] DEZENAS
);

  wire comparador_6_1_out_2, comparador_10_1_out_2, or_1_out, or_2_out;

  SOMADOR_DE_UM somador_de_um_1 (.CLK(CLK), .ENABLE(ENABLE), .PRESET(PRESET), .CLEAR(or_1_out), .SAIDA(UNIDADES));
  or or_1 (or_1_out, CLEAR, comparador_10_1_out_2);
  COMPARADOR_10 comparador_10_1 (.in_1(UNIDADES), .out_2(comparador_10_1_out_2));
  SOMADOR_DE_UM somador_de_um_2 (
    .CLK(comparador_10_1_out_2), .ENABLE(ENABLE), .PRESET(PRESET), .CLEAR(or_2_out), .SAIDA(DEZENAS));
  or or_2 (or_2_out, CLEAR, comparador_6_1_out_2);
  COMPARADOR_6 comparador_6_1 (.in_1(DEZENAS), .out_2(comparador_6_1_out_2));
endmodule

module IGUAL (
  input  [3:0] in_1,
  input  [3:0] in_2,
  output out_3
);

  wire xnor_1_out, xnor_2_out, xnor_3_out, xnor_4_out;

  xnor xnor_1 (xnor_1_out, in_1[0], in_2[0]);
  xnor xnor_2 (xnor_2_out, in_1[1], in_2[1]);
  xnor xnor_3 (xnor_3_out, in_1[2], in_2[2]);
  xnor xnor_4 (xnor_4_out, in_1[3], in_2[3]);
  and and_1 (out_3, xnor_1_out, xnor_2_out, xnor_3_out, xnor_4_out);
endmodule

// 10
module COMPARADOR_10 (
  input  [3:0] in_1,
  output out_2
);

  IGUAL igual_1 (.in_1(in_1), .in_2(4'b1010), .out_3(out_2));
endmodule

// 6
module COMPARADOR_6 (
  input  [3:0] in_1,
  output out_2
);

  IGUAL igual_1 (.in_1(in_1), .in_2(4'b0110), .out_3(out_2));
endmodule

module CRONOMETRO_1_HORA (
  input  CLK,
  input  ENABLE,
  input  PRESET,
  input  CLEAR,
  output [3:0] UNIDADES_SEGUNDOS,
  output [3:0] DEZENAS_SEGUNDOS,
  output [3:0] UNIDADES_MINUTOS,
  output [3:0] DEZENAS_MINUTOS
);

  wire comparador_6_1_out_2, comparador_6_2_out_2, comparador_10_1_out_2, comparador_10_2_out_2, or_1_out,
       or_2_out, or_3_out, or_4_out;

  SOMADOR_DE_UM somador_de_um_1 (
    .CLK(CLK), .ENABLE(ENABLE), .PRESET(PRESET), .CLEAR(or_1_out), .SAIDA(UNIDADES_SEGUNDOS));
  or or_1 (or_1_out, CLEAR, comparador_10_1_out_2);
  COMPARADOR_10 comparador_10_1 (.in_1(UNIDADES_SEGUNDOS), .out_2(comparador_10_1_out_2));
  SOMADOR_DE_UM somador_de_um_2 (
    .CLK(comparador_10_1_out_2), .ENABLE(ENABLE), .PRESET(PRESET), .CLEAR(or_2_out), .SAIDA(DEZENAS_SEGUNDOS));
  or or_2 (or_2_out, CLEAR, comparador_6_1_out_2);
  COMPARADOR_6 comparador_6_1 (.in_1(DEZENAS_SEGUNDOS), .out_2(comparador_6_1_out_2));
  SOMADOR_DE_UM somador_de_um_3 (
    .CLK(comparador_6_1_out_2), .ENABLE(ENABLE), .PRESET(PRESET), .CLEAR(or_3_out), .SAIDA(UNIDADES_MINUTOS));
  or or_3 (or_3_out, CLEAR, comparador_10_2_out_2);
  COMPARADOR_10 comparador_10_2 (.in_1(UNIDADES_MINUTOS), .out_2(comparador_10_2_out_2));
  SOMADOR_DE_UM somador_de_um_4 (
    .CLK(comparador_10_2_out_2), .ENABLE(ENABLE), .PRESET(PRESET), .CLEAR(or_4_out), .SAIDA(DEZENAS_MINUTOS));
  or or_4 (or_4_out, CLEAR, comparador_6_2_out_2);
  COMPARADOR_6 comparador_6_2 (.in_1(DEZENAS_MINUTOS), .out_2(comparador_6_2_out_2));
endmodule
