// Logisim project circuito.circ as structural Verilog: 9 circuits, main circuit main
module main (
  input  in_1,
  input  in_2,
  input  in_3,
  input  in_4,
  input  in_5,
  input  in_6,
  input  in_7,
  input  in_8,
  input  Jogador_atual,
  input  Jogar
);

  wire decodificador_1_a, decodificador_1_b, decodificador_1_c, decodificador_1_d, decodificador_1_e,
       decodificador_1_f, decodificador_1_g, decodificador_2_a, decodificador_2_b, decodificador_2_c,
       decodificador_2_d, decodificador_2_e, decodificador_2_f, decodificador_2_g, game_1_igual,
       game_1_maior, game_1_menor;

  decodificador decodificador_1 (
    .A0(in_1), .A1(in_2), .A2(in_3), .A3(in_4), .a(decodificador_1_a), .b(decodificador_1_b),
    .c(decodificador_1_c), .d(decodificador_1_d), .e(decodificador_1_e), .f(decodificador_1_f),
    .g(decodificador_1_g));
  decodificador decodificador_2 (
    .A0(in_5), .A1(in_6), .A2(in_7), .A3(in_8), .a(decodificador_2_a), .b(decodificador_2_b),
    .c(decodificador_2_c), .d(decodificador_2_d), .e(decodificador_2_e), .f(decodificador_2_f),
    .g(decodificador_2_g));
  _7_Segment_Display u_7_segment_display_1 (
    .g(decodificador_1_g), .f(decodificador_1_f), .a(decodificador_1_a), .b(decodificador_1_b),
    .e(decodificador_1_e), .d(decodificador_1_d), .c(decodificador_1_c));  // open: dp
  _7_Segment_Display u_7_segment_display_2 (
    .g(decodificador_2_g), .f(decodificador_2_f), .a(decodificador_2_a), .b(decodificador_2_b),
    .e(decodificador_2_e), .d(decodificador_2_d), .c(decodificador_2_c));  // open: dp
  game game_1 (
    .A3(in_1), .A2(in_2), .A1(in_3), .A0(in_4), .B3(in_5), .B2(in_6), .B1(in_7), .B0(in_8),
    .Seletor(Jogador_atual), .Power(Jogar), .Maior(game_1_maior), .igual(game_1_igual), .Menor(game_1_menor));
  LED led_1 (.in(game_1_maior));
  LED led_2 (.in(game_1_igual));
  LED led_3 (.in(game_1_menor));

  // Notes on the sheet:
  //   Jogador 0
  //   Jogador 1
  //   Palpite do
  //   Jogador 0
  //   Palpite do
  //   Jogador 1
  //   Maior
  //   igual
  //   Menor
endmodule

module decodificador (
  input  A0,
  input  A1,
  input  A2,
  input  A3,
  output a,
  output b,
  output c,
  output d,
  output e,
  output f,
  output g
);

  wire and_1_out, and_2_out, and_3_out, and_4_out, and_5_out, and_6_out, and_7_out, and_8_out, and_9_out,
       and_10_out, and_11_out, and_12_out, and_13_out, and_14_out, and_15_out, and_16_out, and_17_out,
       and_18_out, and_19_out, and_20_out, and_21_out, and_22_out, and_23_out, and_24_out, and_25_out,
       and_26_out, and_27_out, and_28_out, and_29_out, and_30_out, and_31_out, and_32_out, and_33_out,
       and_34_out, and_35_out, not_1_out, not_2_out, not_3_out, not_4_out, not_5_out, not_6_out, not_7_out,
       not_8_out, not_9_out, not_10_out, not_11_out, not_12_out, not_13_out, not_14_out, not_15_out,
       not_16_out, not_17_out, not_18_out, not_19_out, not_20_out, not_21_out, not_22_out, not_23_out,
       not_24_out, not_25_out, not_26_out, not_27_out, not_28_out, not_29_out, not_30_out, not_31_out,
       not_32_out, not_33_out, not_34_out, not_35_out, not_36_out, not_37_out, not_38_out, not_39_out,
       not_40_out, not_41_out, not_42_out, not_43_out;

  not not_1 (not_1_out, A1);
  and and_1 (and_1_out, not_1_out, not_2_out);
  not not_2 (not_2_out, A3);
  not not_3 (not_3_out, A0);
  and and_2 (and_2_out, not_3_out, A2);
  not not_4 (not_4_out, A0);
  and and_3 (and_3_out, not_4_out, A1, A3);
  and and_4 (and_4_out, A1, A2);
  and and_5 (and_5_out, A0, not_5_out, not_6_out);
  not not_5 (not_5_out, A1);
  not not_6 (not_6_out, A2);
  and and_6 (and_6_out, A0, not_7_out);
  not not_7 (not_7_out, A3);
  not not_8 (not_8_out, A0);
  and and_7 (and_7_out, not_8_out, not_9_out);
  not not_9 (not_9_out, A1);
  not not_10 (not_10_out, A0);
  and and_8 (and_8_out, not_10_out, not_11_out, not_12_out);
  not not_11 (not_11_out, A2);
  not not_12 (not_12_out, A3);
  not not_13 (not_13_out, A1);
  and and_9 (and_9_out, not_13_out, not_14_out);
  not not_14 (not_14_out, A3);
  not not_15 (not_15_out, A0);
  and and_10 (and_10_out, not_15_out, A2, A3);
  not not_16 (not_16_out, A2);
  and and_11 (and_11_out, A0, not_16_out, A3);
  not not_17 (not_17_out, A0);
  and and_12 (and_12_out, not_17_out, not_18_out);
  not not_18 (not_18_out, A2);
  not not_19 (not_19_out, A0);
  and and_13 (and_13_out, not_19_out, A3);
  not not_20 (not_20_out, A2);
  and and_14 (and_14_out, not_20_out, A3);
  not not_21 (not_21_out, A0);
  and and_15 (and_15_out, not_21_out, A1);
  and and_16 (and_16_out, A0, not_22_out);
  not not_22 (not_22_out, A1);
  not not_23 (not_23_out, A0);
  and and_17 (and_17_out, not_23_out, not_24_out, not_25_out);
  not not_24 (not_24_out, A1);
  not not_25 (not_25_out, A3);
  not not_26 (not_26_out, A1);
  and and_18 (and_18_out, not_26_out, A2, A3);
  and and_19 (and_19_out, A1, not_27_out, A3);
  not not_27 (not_27_out, A2);
  and and_20 (and_20_out, A1, A2, not_28_out);
  not not_28 (not_28_out, A3);
  and and_21 (and_21_out, A0, not_29_out);
  not not_29 (not_29_out, A2);
  not not_30 (not_30_out, A1);
  and and_22 (and_22_out, not_30_out, not_31_out);
  not not_31 (not_31_out, A3);
  and and_23 (and_23_out, A2, not_32_out);
  not not_32 (not_32_out, A3);
  and and_24 (and_24_out, A0, A2);
  and and_25 (and_25_out, A0, A1);
  not not_33 (not_33_out, A2);
  and and_26 (and_26_out, not_33_out, not_34_out);
  not not_34 (not_34_out, A3);
  not not_35 (not_35_out, A0);
  and and_27 (and_27_out, not_35_out, A1, not_36_out);
  not not_36 (not_36_out, A2);
  and and_28 (and_28_out, A1, not_37_out);
  not not_37 (not_37_out, A3);
  and and_29 (and_29_out, A0, not_38_out);
  not not_38 (not_38_out, A1);
  and and_30 (and_30_out, A0, A2);
  not not_39 (not_39_out, A1);
  and and_31 (and_31_out, not_39_out, A2);
  and and_32 (and_32_out, A2, not_40_out);
  not not_40 (not_40_out, A3);
  not not_41 (not_41_out, A0);
  and and_33 (and_33_out, not_41_out, A1, not_42_out);
  not not_42 (not_42_out, A2);
  and and_34 (and_34_out, A0, not_43_out);
  not not_43 (not_43_out, A1);
  and and_35 (and_35_out, A0, A3);
  or or_1 (b, and_7_out, and_8_out, and_9_out, and_10_out, and_11_out);
  or or_2 (c, and_12_out, and_13_out, and_14_out, and_15_out, and_16_out);
  or or_3 (d, and_17_out, and_18_out, and_19_out, and_20_out, and_21_out);
  or or_4 (e, and_22_out, and_23_out, and_24_out, and_25_out);
  or or_5 (f, and_26_out, and_27_out, and_28_out, and_29_out, and_30_out);
  or or_6 (g, and_31_out, and_32_out, and_33_out, and_34_out, and_35_out);
  or or_7 (a, and_1_out, and_2_out, and_3_out, and_4_out, and_5_out, and_6_out);

  // Notes on the sheet:
  //   Decodificador para o
  //   display de 7 segmentos
endmodule

module multiplexador (
  input  A,
  input  B,
  input  Seletor,
  input  Power,
  output \Saída 
);

  wire and_1_out, and_2_out;

  and and_1 (and_1_out, A, ~Seletor, Power);  // AND_Gate
  and and_2 (and_2_out, Seletor, B, Power);
  or or_1 (\Saída , and_1_out, and_2_out);
endmodule

module comparador_igual (
  input  A3,
  input  A2,
  input  A1,
  input  A0,
  input  B3,
  input  B2,
  input  B1,
  input  B0,
  output out_9
);

  wire xnor_1_out, xnor_2_out, xnor_3_out, xnor_4_out;

  xnor xnor_1 (xnor_1_out, A3, B3);
  xnor xnor_2 (xnor_2_out, A2, B2);
  xnor xnor_3 (xnor_3_out, A1, B1);
  xnor xnor_4 (xnor_4_out, A0, B0);
  and and_1 (out_9, xnor_1_out, xnor_2_out, xnor_3_out, xnor_4_out);

  // Notes on the sheet:
  //   Compara se dois números (A e B) são iguais
endmodule

module comparador_maior (
  input  A3,
  input  A2,
  input  A1,
  input  A0,
  input  B3,
  input  B2,
  input  B1,
  input  B0,
  output out_9
);

  wire and_1_out, and_2_out, and_3_out, and_4_out, xnor_1_out, xnor_2_out, xnor_3_out;

  and and_1 (and_1_out, A3, ~B3);  // AND_Gate
  xnor xnor_1 (xnor_1_out, A3, B3);
  xnor xnor_2 (xnor_2_out, A2, B2);
  and and_2 (and_2_out, xnor_1_out, A2, ~B2);  // AND_Gate
  and and_3 (and_3_out, xnor_1_out, xnor_2_out, A1, ~B1);  // AND_Gate
  xnor xnor_3 (xnor_3_out, A1, B1);
  and and_4 (and_4_out, xnor_3_out, xnor_1_out, xnor_2_out, A0, ~B0);  // AND_Gate
  or or_1 (out_9, and_1_out, and_2_out, and_3_out, and_4_out);

  // Notes on the sheet:
  //   A3=B3
  //   A2=B2
  //   Compara se A é maior que B
endmodule

module comparador (
  input  A3,
  input  A2,
  input  A1,
  input  A0,
  input  B3,
  input  B2,
  input  B1,
  input  B0,
  output Maior,
  output igual,
  output Menor
);

  comparador_maior comparador_maior_1 (
    .A3(A3), .A2(A2), .A1(A1), .A0(A0), .B3(B3), .B2(B2), .B1(B1), .B0(B0), .out_9(Maior));
  comparador_igual comparador_igual_1 (
    .A3(A3), .A2(A2), .A1(A1), .A0(A0), .B3(B3), .B2(B2), .B1(B1), .B0(B0), .out_9(igual));
  comparador_menor comparador_menor_1 (
    .A3(A3), .A2(A2), .A1(A1), .A0(A0), .B3(B3), .B2(B2), .B1(B1), .B0(B0), .out_9(Menor));
endmodule

module comparador_menor (
  input  A3,
  input  A2,
  input  A1,
  input  A0,
  input  B3,
  input  B2,
  input  B1,
  input  B0,
  output out_9
);

  wire comparador_igual_1_out_9, comparador_maior_1_out_9;

  comparador_igual comparador_igual_1 (
    .A3(A3), .A2(A2), .A1(A1), .A0(A0), .B3(B3), .B2(B2), .B1(B1), .B0(B0), .out_9(comparador_igual_1_out_9));
  comparador_maior comparador_maior_1 (
    .A3(A3), .A2(A2), .A1(A1), .A0(A0), .B3(B3), .B2(B2), .B1(B1), .B0(B0), .out_9(comparador_maior_1_out_9));
  nor nor_1 (out_9, comparador_igual_1_out_9, comparador_maior_1_out_9);
endmodule

module multiplexador_4_bits (
  input  A3,
  input  A2,
  input  A1,
  input  A0,
  input  B3,
  input  B2,
  input  B1,
  input  B0,
  input  Seletor,
  input  Power,
  output out_11,
  output out_12,
  output out_13,
  output out_14
);

  multiplexador multiplexador_1 (.A(A3), .B(B3), .Seletor(Seletor), .Power(Power), .\Saída (out_11));
  multiplexador multiplexador_2 (.A(A2), .B(B2), .Seletor(Seletor), .Power(Power), .\Saída (out_12));
  multiplexador multiplexador_3 (.A(A1), .B(B1), .Seletor(Seletor), .Power(Power), .\Saída (out_13));
  multiplexador multiplexador_4 (.A(A0), .B(B0), .Seletor(Seletor), .Power(Power), .\Saída (out_14));
endmodule

module game (
  input  A3,
  input  A2,
  input  A1,
  input  A0,
  input  B3,
  input  B2,
  input  B1,
  input  B0,
  input  Seletor,
  input  Power,
  output Maior,
  output igual,
  output Menor
);

  wire multiplexador_4_bits_1_out_11, multiplexador_4_bits_1_out_12, multiplexador_4_bits_1_out_13,
       multiplexador_4_bits_1_out_14;

  multiplexador_4_bits multiplexador_4_bits_1 (
    .A3(A3), .A2(A2), .A1(A1), .A0(A0), .B3(B3), .B2(B2), .B1(B1), .B0(B0), .Seletor(Seletor), .Power(Power),
    .out_11(multiplexador_4_bits_1_out_11), .out_12(multiplexador_4_bits_1_out_12),
    .out_13(multiplexador_4_bits_1_out_13), .out_14(multiplexador_4_bits_1_out_14));
  comparador comparador_1 (
    .A3(multiplexador_4_bits_1_out_11), .A2(multiplexador_4_bits_1_out_12),
    .A1(multiplexador_4_bits_1_out_13), .A0(multiplexador_4_bits_1_out_14), .B3(1'b0), .B2(1'b1), .B1(1'b0),
    .B0(1'b1), .Maior(Maior), .igual(igual), .Menor(Menor));

  // Notes on the sheet:
  //   Número mágico
endmodule
